# Fritzing sketch SpectrumLeds (saved by Fritzing 0.9.3b)
breadboards: 1

parts:
  C1 = Capacitor Polarized [package=cpol-radial-1000uf-25v]
  R1 = Resistor [tolerance=±5% resistance=100 package=THT]
  Bauteil1 = Breakout Board for Electret Microphone [part_number=MAX4466]
  U2 = WS2812 RGB LED strip [part_number=WS2812B]
  PS1 = prefix0000 [part_number="5V 20A AC/DC 100W "]
  D1 = Rectifier Diode [part_number=1N4001 package="300 mil [THT]"]
  C2 = Capacitor Polarized [package=cpol-radial-1000uf-25v]
  U1 = ESP32-38PinWide

nets:
  N1: C1.+, Bauteil1.VCC, D1.cathode
  GND: C1.-, Bauteil1.GND, U2.GND, PS1.connector5, C2.-, U1.GND
  N2: R1.Pin_0, U1.GPIO27, U1.GPIO14, U1.GPIO12, U1.GPIO13
  N3: R1.Pin_1, U2.DIN
  N4: Bauteil1.AUD, U1.GPIO36
  VCC: U2.VCC, PS1.connector0, D1.anode, C2.+, U1.VIN
  N5: U1.GPIO39, U1.GPIO34, U1.GPIO35, U1.GPIO32, U1.GPIO33
  N6: U1.GPIO2, U1.GPIO0, U1.GPIO4, U1.GPIO16, U1.GPIO17

custom parts:
  WS2812 RGB LED strip: WS2812 strip
  ESP32-38PinWide: Generic 38-Pin ESP32 with wide format (only access to one side of pins on a breadboard) based on Stephen Lilley's HiLetgo ESP-WROOM-32 ESP32 ESP-32S Development Board.
